# Fritzing sketch Signal_Recorder (saved by Fritzing 0.9.3b)
perfboards: 1

parts:
  パーツ1 = Arduino Uno (Rev3)
  R1 = Photocell (LDR) [package=THT]
  R2 = Photocell (LDR) [package=THT]
  R3 = Photocell (LDR) [package=THT]
  R4 = Resistor [tolerance=±5% resistance=220 package=THT]
  R5 = Resistor [tolerance=±5% resistance=220 package=THT]
  R6 = Resistor [tolerance=±5% resistance=220 package=THT]
  S1 = Pushbutton [package=THT]
  LED2 = LED - 5mm [color="Red (633nm)" package="5 mm [THT]"]
  LED3 = LED - 5mm [color="Red (633nm)" package="5 mm [THT]"]  # not connected
  R8 = Resistor [tolerance=±5% resistance=220 package=THT]
  R9 = Resistor [tolerance=±5% resistance=220 package=THT]
  R10 = Resistor [tolerance=±5% resistance=220 package=THT]

nets:
  N1: パーツ1.A0, R3.pin_0, R4.Pin_0
  N2: パーツ1.D13/SCK, R1.pin_0, R6.Pin_0
  N3: パーツ1.GND, R1.pin_1, R2.pin_1, R3.pin_1, R8.Pin_1
  N4: パーツ1.D6_PWM, R2.pin_0, R5.Pin_0
  N5: パーツ1.5V, R4.Pin_1, R5.Pin_1, R6.Pin_1, S1.leg1
  N6: S1.leg0, R10.Pin_0
  N7: LED2.cathode, R9.Pin_0

// code stored in the sketch: signal_recorder.ino
// ?????????????
// 18,47??????????????????????????????????????

#define data_num 1000

void cdown(unsigned int times);
void send_data(boolean, int);
unsigned int i,t;
boolean digital_data[data_num] = {0};

void setup() {
  t = millis();
  digitalWrite(13,HIGH);
  Serial.begin(9600);
  pinMode(2,INPUT);
  pinMode(4,INPUT);
  pinMode(13,OUTPUT);
//  Serial.println("standingby...");
  while(millis() < t+1000){}
  digitalWrite(13,LOW);
}

void loop() {
  while(digitalRead(2)){
    cdown(3);
    t = millis();
    digitalWrite(13,HIGH);
    i=0;
    while(millis() < t + 1000){
      digital_data[i] = digitalRead(4);
      delay(1);
      i++;
    }
    digitalWrite(13,LOW);
    for(i = 0; i < data_num; i++){
      send_data(digital_data[i]);
    }
    Serial.flush();
    pinMode(12,OUTPUT);
  }
}

void cdown(unsigned int times){
  for(i = 0;i < times;i++){
    t = millis();
    digitalWrite(13,HIGH);
//    Serial.println(3-i);
    while(millis() < t+100){}
    digitalWrite(13,LOW);
//		Serial.println("LOW");
    while(millis() < t+500){}
  }
}

void send_data(boolean d_data){
  Serial.println(d_data);
  delay(10);
}
